// Logisim project 4-bit-cpu-v2.circ as structural Verilog: 10 circuits, main circuit main
module main (
  input  in_1,
  input  in_2,
  input  in_3,
  input  in_4,
  input  RESET
);

  wire BREAK, clock_1_out, counter_2_carry, d_ff_1_q, decoder_1_out0, decoder_1_out1, LDPC, not_1_out,
       not_2_out, or_1_out, RAE, RWRAM, ZE;
  wire [1:0] BUS_MUX, counter_2_q;
  wire [3:0] counter_1_q, CYCLE, multiplexer_1_out, OPCODE, ram_1_data, register_1_q, register_2_q,
       rom_1_data;

  // Probe on LDPC
  not not_1 (not_1_out, LDPC);
  Clock clock_1 (.out(clock_1_out));
  Counter #(.width(4), .max('hf)) counter_1 (
    .load(LDPC), .D(multiplexer_1_out), .count(not_1_out), .Q(counter_1_q), .clk(clock_1_out), .clr(RESET));  // open: carry
  Register #(.width(4)) register_1 (.D(multiplexer_1_out), .en(RAE), .Q(register_1_q), .clk(clock_1_out));  // open: clr
  // Probe on RAE
  RAM #(.addrWidth(4), .dataWidth(4)) ram_1 (
    .addr(register_1_q), .data(ram_1_data), .clk(clock_1_out), .ld(not_2_out));  // open: sel, clr
  not not_2 (not_2_out, RWRAM);
  ROM #(.addrWidth(4), .dataWidth(4)) rom_1 (.addr(counter_1_q), .data(rom_1_data));  // open: sel
  assign ram_1_data = RWRAM ? multiplexer_1_out : 4'bz;  // Controlled_Buffer controlled_buffer_1
  // Probe on RWRAM
  Register #(.width(4)) register_2 (.D(multiplexer_1_out), .en(ZE), .Q(register_2_q), .clk(clock_1_out));  // open: clr
  // Probe on ZE
  Register #(.width(4)) register_3 (.D(rom_1_data), .en(or_1_out), .Q(OPCODE), .clk(clock_1_out));  // open: clr
  Multiplexer #(.select(2), .width(4)) multiplexer_1 (
    .in0(rom_1_data), .in1(ram_1_data), .in2(register_2_q), .out(multiplexer_1_out), .sel(BUS_MUX), .en(1'b1));  // open: in3
  // Probe on BUS_MUX
  Decoder #(.select(4)) decoder_1 (
    .out0(decoder_1_out0), .out1(decoder_1_out1), .sel(OPCODE));  // open: out2, out3, out4, out5, out6, out7, out8, out9, out10, out11, out12, out13, out14, out15, en
  Counter #(.width(2), .max('h3)) counter_2 (
    .Q(counter_2_q), .carry(counter_2_carry), .clk(clock_1_out), .clr(d_ff_1_q));  // open: load, D, count
  or or_1 (or_1_out, d_ff_1_q, decoder_1_out0, counter_2_carry);
  D_Flip_Flop d_ff_1 (.clk(clock_1_out), .D(BREAK), .Q(d_ff_1_q));  // open: Qn, preset, en, reset
  Decoder #(.select(2)) decoder_2 (
    .out0(CYCLE[0]), .out1(CYCLE[1]), .out2(CYCLE[2]), .out3(CYCLE[3]), .sel(counter_2_q));  // open: en
  NOP nop_1 (.CYCLE_IN(CYCLE), .ENABLE(decoder_1_out1));  // open: BUS_CTRL
  LDZ ldz_1 (.CYCLE_IN(CYCLE));  // open: ENABLE, BUS_CTRL
  MOVZ movz_1 ();  // open: CYCLE_IN, ENABLE
  ALU alu_1 ();  // open: A, B, CTRL, ENABLE, CIN, BIN, ALU_OUT, ALU_STATUS, DIV_REM
  Multiplexer #(.select(4)) multiplexer_2 (
    .out(LDPC), .sel(OPCODE));  // open: in0, in1, in2, in3, in4, in5, in6, in7, in8, in9, in10, in11, in12, in13, in14, in15, en
  // OR_Gate or_2 has open pins: out=ZE
  // OR_Gate or_3 has open pins: out=RWRAM
  // OR_Gate or_4 has open pins: out=RAE
  // OR_Gate or_5 has open pins: out=BUS_MUX[0]
  // OR_Gate or_6 has open pins: out=BUS_MUX[1]
  // OR_Gate or_7 has open pins: out=BREAK

  // Notes on the sheet:
  //   LDPC
  //   RAM
  //   PROG MEM
  //   contents of rom_1 (hex, n*v repeats v):
  //   1 1 5 4 5 6 7 1 9 a b c d e f
  //   R/W RAM
  //   Z REG
  //   INSTRUCTION REG
  //   break cycle logic
  //   CPU CYCLE
endmodule

module NOP (
  input  [3:0] CYCLE_IN,
  input  ENABLE,
  output [4:0] BUS_CTRL
);

  Pull_Resistor pull_resistor_1 (.node(CYCLE_IN[3]));
  Pull_Resistor pull_resistor_2 (.node(BUS_CTRL[4]));

  assign BUS_CTRL[3:0] = {4{BUS_CTRL[4]}};
  assign CYCLE_IN[2:0] = {3{CYCLE_IN[3]}};
  assign ENABLE = CYCLE_IN[3];

  // Notes on the sheet:
  //   LDPCO
  //   ZE
  //   RWRAM
  //   BMX0
  //   RAEO
  //   BMX0
  //   BMX1
  //   BRK
endmodule

module MOVZ (
  input  [3:0] CYCLE_IN,
  input  ENABLE
);

  wire controlled_buffer_6_out, pull_resistor_2_node, pull_resistor_3_node;

  Controlled_Buffer controlled_buffer_1 (.in(CYCLE_IN[0]), .en(ENABLE));  // open: out
  Controlled_Buffer controlled_buffer_2 (.in(CYCLE_IN[1]), .en(ENABLE));  // open: out
  Controlled_Buffer controlled_buffer_3 (.in(CYCLE_IN[2]), .en(ENABLE));  // open: out
  Controlled_Buffer controlled_buffer_4 (.in(CYCLE_IN[3]), .en(ENABLE));  // open: out
  Pull_Resistor pull_resistor_1 ();  // open: node
  Controlled_Buffer controlled_buffer_5 (.en(pull_resistor_2_node));  // open: in, out
  Pull_Resistor pull_resistor_2 (.node(pull_resistor_2_node));
  Controlled_Buffer controlled_buffer_6 (.out(controlled_buffer_6_out), .en(pull_resistor_3_node));  // open: in
  Pull_Resistor pull_resistor_3 (.node(pull_resistor_3_node));

  // Notes on the sheet:
  //   INSUTRCTION EXECUTE STAGE
  //   CONTROL WORD
  //   LDPCO
  //   ZE
  //   RWRAM
  //   BMX0
  //   RAEO
  //   BMX0
  //   BMX1
  //   BRK
endmodule

module LDZ (
  input  [3:0] CYCLE_IN,
  input  ENABLE,
  output [4:0] BUS_CTRL
);

  wire controlled_buffer_1_out, controlled_buffer_2_out, controlled_buffer_3_out, controlled_buffer_4_out;

  assign controlled_buffer_1_out = ENABLE ? CYCLE_IN[0] : 1'bz;  // Controlled_Buffer controlled_buffer_1
  assign controlled_buffer_2_out = ENABLE ? CYCLE_IN[1] : 1'bz;  // Controlled_Buffer controlled_buffer_2
  assign controlled_buffer_3_out = ENABLE ? CYCLE_IN[2] : 1'bz;  // Controlled_Buffer controlled_buffer_3
  assign controlled_buffer_4_out = ENABLE ? CYCLE_IN[3] : 1'bz;  // Controlled_Buffer controlled_buffer_4
  Pull_Resistor pull_resistor_1 (.node(BUS_CTRL[4]));

  assign BUS_CTRL[3:0] = {4{BUS_CTRL[4]}};

  // Notes on the sheet:
  //   LDPCO
  //   ZE
  //   RWRAM
  //   BMX0
  //   RAEO
  //   BMX0
  //   BMX1
  //   BRK
endmodule

module NOP_COPY (
  input  CS0,
  input  CS1,
  input  CS2,
  input  CS3,
  input  ENABLE,
  output LDPCO,
  output ZE,
  output RWRAM,
  output RAEO,
  output BMX0,
  output BMX1,
  output BRK
);


  assign BMX0 = 1'b0;
  assign BMX1 = 1'b0;
  assign BRK = 1'b0;
  assign CS1 = CS0;
  assign CS2 = CS0;
  assign CS3 = CS0;
  assign ENABLE = CS0;
  assign LDPCO = 1'b0;
  assign RAEO = 1'b0;
  assign RWRAM = 1'b0;
  assign ZE = 1'b0;
  // also tied to GND on the sheet: CS0

  // Notes on the sheet:
  //   LDPCO
  //   ZE
  //   RWRAM
  //   BMX0
  //   RAEO
  //   BMX0
  //   BMX1
  //   BRK
endmodule

module ALU (
  input  [7:0] A,
  input  [7:0] B,
  input  [3:0] CTRL,
  input  ENABLE,
  input  CIN,
  input  BIN,
  output [7:0] ALU_OUT,
  output [7:0] ALU_STATUS,
  output [7:0] DIV_REM
);

  wire [7:0] A0, A1, A2, A3, A4, A5, A6, A7, A8, A9, B0, B1, B2, B3, B4, B5, B6, B7, B8, B9, O0, O1, O2, O3,
       O4, O5, O6, O7, O8, O9, pull_resistor_1_node, pull_resistor_2_node;

  Pull_Resistor pull_resistor_1 (.node(pull_resistor_1_node));
  Demultiplexer #(.select(4), .width(8)) demultiplexer_1 (
    .out0(A0), .out1(A1), .out2(A2), .out3(A3), .out4(A4), .out5(A5), .out6(A6), .out7(A7), .out8(A8),
    .out9(A9), .in(pull_resistor_1_node), .sel(CTRL));  // open: out10, out11, out12, out13, out14, out15, en
  assign pull_resistor_1_node = ENABLE ? A : 8'bz;  // Controlled_Buffer controlled_buffer_1
  Pull_Resistor pull_resistor_2 (.node(pull_resistor_2_node));
  Demultiplexer #(.select(4), .width(8)) demultiplexer_2 (
    .out0(B0), .out1(B1), .out2(B2), .out3(B3), .out4(B4), .out5(B5), .out6(B6), .out7(B7), .out8(B8),
    .out9(B9), .in(pull_resistor_2_node), .sel(CTRL));  // open: out10, out11, out12, out13, out14, out15, en
  assign pull_resistor_2_node = ENABLE ? B : 8'bz;  // Controlled_Buffer controlled_buffer_2
  Multiplier multiplier_1 (.a(B2), .b(A2), .out(O2));  // open: cin, cout
  Divider divider_1 (.a(A3), .b(B3), .out(O3), .rem(DIV_REM));  // open: upper
  _8BIT_NOT u_8bit_not_1 (.A(A4), .B(B4), .OUT(O4));
  _8BIT_AND u_8bit_and_1 (.A(A5), .B(B5), .OUT(O5));
  _8BIT_OR u_8bit_or_1 (.A(A6), .B(B6), .OUT(O6));
  _8BIT_XOR u_8bit_xor_1 (.A(A7), .B(B7), .OUT(O7));
  Comparator comparator_1 (.a(A8), .b(B8), .gt(O8[0]), .eq(O8[1]), .lt(O8[2]));
  Adder adder_1 (.a(A0), .b(B0), .out(O0), .cin(CIN), .cout(ALU_STATUS[0]));
  Subtractor subtractor_1 (.a(A1), .b(B1), .out(O1), .bin(BIN), .bout(ALU_STATUS[1]));
  Multiplexer #(.select(4), .width(8)) multiplexer_1 (
    .in0(O0), .in1(O1), .in2(O2), .in3(O3), .in4(O4), .in5(O5), .in6(O6), .in7(O7), .in8(O8), .in9(O9),
    .out(ALU_OUT), .sel(CTRL));  // open: in10, in11, in12, in13, in14, in15, en
  Comparator comparator_2 (.a({8{1'b0}}), .b(ALU_OUT), .eq(ALU_STATUS[2]));  // open: gt, lt
  Pull_Resistor pull_resistor_3 (.node(ALU_OUT));
  // Probe on ALU_OUT

  // Other names for the same wires on the sheet: ALU_CTRL[3:0] = CTRL; COUT = ALU_STATUS[0]; BOUT = ALU_STATUS[1];
  //   ZERO = ALU_STATUS[2]; REM[7:0] = DIV_REM

  // Notes on the sheet:
  //   VALUES
  //   ALU CONTROL
  //   OUTPUTS
endmodule

// OR
module _8BIT_OR (
  input  [7:0] A,
  input  [7:0] B,
  output [7:0] OUT
);

  or or_1 (OUT[0], A[0], B[0]);
  or or_2 (OUT[1], A[1], B[1]);
  or or_3 (OUT[2], A[2], B[2]);
  or or_4 (OUT[3], A[3], B[3]);
  or or_5 (OUT[4], A[4], B[4]);
  or or_6 (OUT[5], B[5], A[5]);
  or or_7 (OUT[6], A[6], B[6]);
  or or_8 (OUT[7], A[7], B[7]);
endmodule

// AND
module _8BIT_AND (
  input  [7:0] A,
  input  [7:0] B,
  output [7:0] OUT
);

  and and_1 (OUT[0], A[0], B[0]);
  and and_2 (OUT[1], A[1], B[1]);
  and and_3 (OUT[2], A[2], B[2]);
  and and_4 (OUT[3], A[3], B[3]);
  and and_5 (OUT[4], A[4], B[4]);
  and and_6 (OUT[5], B[5], A[5]);
  and and_7 (OUT[6], A[6], B[6]);
  and and_8 (OUT[7], A[7], B[7]);
endmodule

// NOT
module _8BIT_NOT (
  input  [7:0] A,
  input  [7:0] B,
  output [7:0] OUT
);

  assign OUT = ~A;  // NOT_Gate not_1, 8 bits wide

  // Notes on the sheet:
  //   LDPCO
  //   ZE
  //   RWRAM
  //   BMX0
  //   RAEO
  //   BMX0
  //   BMX1
  //   BRK
endmodule

// XOR
module _8BIT_XOR (
  input  [7:0] A,
  input  [7:0] B,
  output [7:0] OUT
);

  xor xor_1 (OUT[0], A[0], B[0]);
  xor xor_2 (OUT[1], A[1], B[1]);
  xor xor_3 (OUT[2], A[2], B[2]);
  xor xor_4 (OUT[3], A[3], B[3]);
  xor xor_5 (OUT[4], A[4], B[4]);
  xor xor_6 (OUT[5], B[5], A[5]);
  xor xor_7 (OUT[6], A[6], B[6]);
  xor xor_8 (OUT[7], A[7], B[7]);
endmodule
